# Fritzing sketch Node_Cisterna (saved by Fritzing 0.9.2b)
breadboards: 1

parts:
  R1 = Resistor [tolerance=±5% resistance=220 package=THT]
  R2 = Resistor [tolerance=±5% resistance=220 package=THT]
  R3 = Resistor [tolerance=±5% resistance=220 package=THT]
  U2 = NodeMCU V1.0
  Componente2 = SRF05 Ultrasonic Rangefinder
  Power_plug1 = Power plug

nets:
  N1: R1.Pin_0, R2.Pin_1
  GND: R1.Pin_1, U2.GND, Componente2.GND, Power_plug1.GND
  N2: R2.Pin_0, R3.Pin_1, U2.D3
  N3: R3.Pin_0, Componente2.Echo
  N4: U2.D4, Componente2.Trig
  VCC: U2.Vin, Componente2.VCC, Power_plug1.VCC

notes:
  Fonte 5V

custom parts:
  NodeMCU V1.0: ESP8266 based NodeMCU
