# Fritzing sketch Node_Cisterna_Transistor (saved by Fritzing 0.9.2b)
breadboards: 1

parts:
  R1 = Resistor [tolerance=±5% resistance=220 package=THT]
  R2 = Resistor [tolerance=±5% resistance=220 package=THT]
  R3 = Resistor [tolerance=±5% resistance=220 package=THT]
  U2 = NodeMCU V1.0
  Componente2 = SRF05 Ultrasonic Rangefinder
  Power_plug1 = Power plug
  Q1 = NPN-Transistor [package="TO92 [THT]"]
  R4 = Resistor [tolerance=±5% resistance=220 package=THT]
  R5 = Resistor [tolerance=±5% resistance=220 package=THT]

nets:
  N1: R1.Pin_0, R2.Pin_1
  GND: R1.Pin_1, U2.GND, Componente2.connector11, Power_plug1.GND
  N2: R2.Pin_0, R3.Pin_1, U2.D3
  N3: R3.Pin_0, Componente2.connector10
  N4: U2.D4, R4.Pin_0
  VIN: U2.Vin, Componente2.connector8, Power_plug1.VCC, R5.Pin_0
  N5: Componente2.connector9, Q1.E
  N6: Q1.B, R4.Pin_1
  N7: Q1.C, R5.Pin_1

notes:
  Fonte 5V

custom parts:
  NodeMCU V1.0: ESP8266 based NodeMCU
